# Fritzing sketch Startlichter (saved by Fritzing 0.9.3b)
circuit board: 6.88566cm x 5.36311cm
breadboards: 1

parts:
  Bauteil1 = Arduino Uno (Rev3)
  LED2 = LED - 5mm [color="Red (633nm)" package="5 mm [THT]"]
  LED3 = LED - 5mm [color="Red (633nm)" package="5 mm [THT]"]
  LED4 = LED - 5mm [color="Red (633nm)" package="5 mm [THT]"]
  LED5 = LED - 5mm [color="Red (633nm)" package="5 mm [THT]"]
  LED6 = LED - 5mm [color="Red (633nm)" package="5 mm [THT]"]
  R1 = Resistor [tolerance=±5% resistance=10k package=THT]
  S1 = Pushbutton [package="[THT]"]
  R2 = Resistor [tolerance=±5% resistance=100 package=THT]
  R3 = Resistor [tolerance=±5% resistance=100 package=THT]
  R4 = Resistor [tolerance=±5% resistance=100 package=THT]
  R5 = Resistor [tolerance=±5% resistance=100 package=THT]
  R6 = Resistor [tolerance=±5% resistance=100 package=THT]

nets:
  N1: Bauteil1.D8, R3.Pin_0
  N2: Bauteil1.D9_PWM, R2.Pin_0
  N3: Bauteil1.D2, R1.Pin_0, S1.Pin_3, S1.Pin_4
  N4: Bauteil1.D5_PWM, R6.Pin_0
  N5: Bauteil1.D6_PWM, R5.Pin_0
  N6: Bauteil1.D7, R4.Pin_0
  N7: Bauteil1.5V, S1.Pin_1, S1.Pin_2
  N8: Bauteil1.GND, LED2.cathode, LED3.cathode, LED4.cathode, LED5.cathode, LED6.cathode, R1.Pin_1
  N9: LED2.anode, R2.Pin_1
  N10: LED3.anode, R3.Pin_1
  N11: LED4.anode, R4.Pin_1
  N12: LED5.anode, R5.Pin_1
  N13: LED6.anode, R6.Pin_1

notes:
  CHASER_LIGHTS

// code stored in the sketch: ChaserLights.ino
/*
  chaserlights
  
  This example is part of the Fritzing Creator Kit: www.fritzing.org/creator-kit.
*/

int pinsCount=8;                        // declaring the integer variable pinsCount
int pins[] = {2,3,4,5,6,7,8,9};          // declaring the array pins[]

void setup() {                
  for (int i=0; i<pinsCount; i=i+1){    // counting the variable i from 0 to 7
    pinMode(pins[i], OUTPUT);            // initialising the pin at index i of the array of pins as OUTPUT
  }
}

void loop() {
  for (int i=0; i<pinsCount; i=i+1){    // chasing right
    digitalWrite(pins[i], HIGH);         // switching the LED at index i on
    delay(100);                          // stopping the program for 100 milliseconds
    digitalWrite(pins[i], LOW);          // switching the LED at index i off
  }
  for (int i=pinsCount-1; i>0; i=i-1){   // chasing left (except the outer leds)
    digitalWrite(pins[i], HIGH);         // switching the LED at index i on
    delay(100);                          // stopping the program for 100 milliseconds
    digitalWrite(pins[i], LOW);          // switching the LED at index i off
  }
}
